// Logisim project 0 counter.circ as structural Verilog: 2 circuits, main circuit main
module main (
  input  [7:0] in_1
);

  wire [3:0] zero_counter_1_zeroes;

  Hex_Digit_Display hex_digit_display_1 (.value(zero_counter_1_zeroes));  // open: dp
  zero_counter zero_counter_1 (.in(in_1), .zeroes(zero_counter_1_zeroes));
endmodule

module zero_counter (
  input  [7:0] in,
  output [3:0] zeroes
);

  wire [3:0] adder_1_out, adder_2_out, adder_3_out, adder_4_out, adder_5_out, adder_6_out, adder_7_out;

  Hex_Digit_Display hex_digit_display_1 (.value(in[7:4]));  // open: dp
  Hex_Digit_Display hex_digit_display_2 (.value(in[3:0]));  // open: dp
  Adder #(.width(4)) adder_1 (.a({3'b000, in[0]}), .b({3'b000, in[1]}), .out(adder_1_out));  // open: cin, cout
  Adder #(.width(4)) adder_2 (.a({3'b000, in[2]}), .b({3'b000, in[3]}), .out(adder_2_out));  // open: cin, cout
  Adder #(.width(4)) adder_3 (.a({3'b000, in[4]}), .b({3'b000, in[5]}), .out(adder_3_out));  // open: cin, cout
  Adder #(.width(4)) adder_4 (.a({3'b000, in[6]}), .b({3'b000, in[7]}), .out(adder_4_out));  // open: cin, cout
  Adder #(.width(4)) adder_5 (.a(adder_1_out), .b(adder_2_out), .out(adder_5_out));  // open: cin, cout
  Adder #(.width(4)) adder_6 (.a(adder_3_out), .b(adder_4_out), .out(adder_6_out));  // open: cin, cout
  Adder #(.width(4)) adder_7 (.a(adder_5_out), .b(adder_6_out), .out(adder_7_out));  // open: cin, cout
  Hex_Digit_Display hex_digit_display_3 (.value(zeroes));  // open: dp
  Subtractor #(.width(4)) subtractor_1 (.a(4'b1000), .b(adder_7_out), .out(zeroes));  // open: bin, bout
endmodule
