// Logisim project 4 bit bcd adder.circ as structural Verilog: 3 circuits, main circuit main
module main (
  input  [15:0] in_1,
  input  [15:0] in_2
);

  wire [19:0] n4_bit_bcd_adder_1_out_3;

  Hex_Digit_Display hex_digit_display_1 (.value(in_1[15:12]));  // open: dp
  Hex_Digit_Display hex_digit_display_2 (.value(in_1[11:8]));  // open: dp
  Hex_Digit_Display hex_digit_display_3 (.value(in_1[3:0]));  // open: dp
  Hex_Digit_Display hex_digit_display_4 (.value(in_1[7:4]));  // open: dp
  Hex_Digit_Display hex_digit_display_5 (.value(in_2[15:12]));  // open: dp
  Hex_Digit_Display hex_digit_display_6 (.value(in_2[11:8]));  // open: dp
  Hex_Digit_Display hex_digit_display_7 (.value(in_2[7:4]));  // open: dp
  _4_bit_bcd_adder u_4_bit_bcd_adder_1 (.A(in_1), .B(in_2), .out_3(n4_bit_bcd_adder_1_out_3));
  Hex_Digit_Display hex_digit_display_8 (.value(in_2[3:0]));  // open: dp
  Hex_Digit_Display hex_digit_display_9 (.value(n4_bit_bcd_adder_1_out_3[15:12]));  // open: dp
  Hex_Digit_Display hex_digit_display_10 (.value(n4_bit_bcd_adder_1_out_3[19:16]));  // open: dp
  Hex_Digit_Display hex_digit_display_11 (.value(n4_bit_bcd_adder_1_out_3[11:8]));  // open: dp
  Hex_Digit_Display hex_digit_display_12 (.value(n4_bit_bcd_adder_1_out_3[7:4]));  // open: dp
  Hex_Digit_Display hex_digit_display_13 (.value(n4_bit_bcd_adder_1_out_3[3:0]));  // open: dp
endmodule

module _1_bit_bcd_adder (
  input  [3:0] A,
  input  c_in,
  input  [3:0] B,
  output c_out,
  output [3:0] out
);

  wire [4:0] adder_1_out;
  wire [4:1] divider_1_out;
  wire [4:4] divider_1_rem;

  Hex_Digit_Display hex_digit_display_1 (.value(A));  // open: dp
  Hex_Digit_Display hex_digit_display_2 (.value(B));  // open: dp
  Adder #(.width(5)) adder_1 (.a({1'b0, A}), .b({1'b0, B}), .out(adder_1_out), .cin(c_in));  // open: cout
  Divider #(.width(5)) divider_1 (
    .a(adder_1_out), .b(5'b01010), .out({divider_1_out, c_out}), .rem({divider_1_rem[4], out}));  // open: upper
  Hex_Digit_Display hex_digit_display_3 (.value(out));  // open: dp
endmodule

module _4_bit_bcd_adder (
  input  [15:0] A,
  input  [15:0] B,
  output [19:0] out_3
);

  wire n1_bit_bcd_adder_1_c_out, n1_bit_bcd_adder_2_c_out, n1_bit_bcd_adder_3_c_out;

  Hex_Digit_Display hex_digit_display_1 (.value(A[15:12]));  // open: dp
  Hex_Digit_Display hex_digit_display_2 (.value(A[11:8]));  // open: dp
  Hex_Digit_Display hex_digit_display_3 (.value(A[7:4]));  // open: dp
  Hex_Digit_Display hex_digit_display_4 (.value(A[3:0]));  // open: dp
  Hex_Digit_Display hex_digit_display_5 (.value(B[11:8]));  // open: dp
  Hex_Digit_Display hex_digit_display_6 (.value(B[15:12]));  // open: dp
  Hex_Digit_Display hex_digit_display_7 (.value(B[7:4]));  // open: dp
  Hex_Digit_Display hex_digit_display_8 (.value(B[3:0]));  // open: dp
  _1_bit_bcd_adder u_1_bit_bcd_adder_1 (
    .A(A[3:0]), .B(B[3:0]), .c_out(n1_bit_bcd_adder_1_c_out), .out(out_3[3:0]));  // open: c_in
  _1_bit_bcd_adder u_1_bit_bcd_adder_2 (
    .A(A[7:4]), .B(B[7:4]), .c_in(n1_bit_bcd_adder_1_c_out), .c_out(n1_bit_bcd_adder_2_c_out),
    .out(out_3[7:4]));
  _1_bit_bcd_adder u_1_bit_bcd_adder_3 (
    .A(A[11:8]), .B(B[11:8]), .c_in(n1_bit_bcd_adder_2_c_out), .c_out(n1_bit_bcd_adder_3_c_out),
    .out(out_3[11:8]));
  _1_bit_bcd_adder u_1_bit_bcd_adder_4 (
    .A(A[15:12]), .B(B[15:12]), .c_in(n1_bit_bcd_adder_3_c_out), .c_out(out_3[16]), .out(out_3[15:12]));
  Hex_Digit_Display hex_digit_display_9 (.value({3'b000, out_3[16]}));  // open: dp
  Hex_Digit_Display hex_digit_display_10 (.value(out_3[15:12]));  // open: dp
  Hex_Digit_Display hex_digit_display_11 (.value(out_3[11:8]));  // open: dp
  Hex_Digit_Display hex_digit_display_12 (.value(out_3[3:0]));  // open: dp
  Hex_Digit_Display hex_digit_display_13 (.value(out_3[7:4]));  // open: dp

  assign out_3[19:17] = 3'b000;
endmodule
