// Logisim project ALU.circ as structural Verilog: 2 circuits, main circuit main
module main (
  input  [7:0] A,
  input  [7:0] B,
  input  [2:0] sel
);

  wire [7:0] alu_1_output;

  Hex_Digit_Display hex_digit_display_1 (.value(A[3:0]));  // open: dp
  Hex_Digit_Display hex_digit_display_2 (.value(A[7:4]));  // open: dp
  Hex_Digit_Display hex_digit_display_3 (.value(B[3:0]));  // open: dp
  Hex_Digit_Display hex_digit_display_4 (.value(B[7:4]));  // open: dp
  Hex_Digit_Display hex_digit_display_5 (.value({1'b0, sel}));  // open: dp
  ALU alu_1 (.A(A), .B(B), .sel(sel), .\output (alu_1_output));
  Hex_Digit_Display hex_digit_display_6 (.value(alu_1_output[3:0]));  // open: dp
  Hex_Digit_Display hex_digit_display_7 (.value(alu_1_output[7:4]));  // open: dp
endmodule

module ALU (
  input  [7:0] A,
  input  [7:0] B,
  input  [2:0] sel,
  output [7:0] \output 
);

  wire [7:0] adder_1_out, adder_2_out, and_1_out, not_1_out, or_1_out, subtractor_1_out, subtractor_2_out,
       xor_1_out;

  Adder adder_1 (.a(A), .b(B), .out(adder_1_out));  // open: cin, cout
  Subtractor subtractor_1 (.a(A), .b(B), .out(subtractor_1_out));  // open: bin, bout
  Adder adder_2 (.a(A), .b(8'h1), .out(adder_2_out));  // open: cin, cout
  Subtractor subtractor_2 (.a(A), .b(8'h1), .out(subtractor_2_out));  // open: bin, bout
  assign and_1_out = A & B;  // AND_Gate and_1, 8 bits wide
  assign or_1_out = A | B;  // OR_Gate or_1, 8 bits wide
  assign not_1_out = ~A;  // NOT_Gate not_1, 8 bits wide
  assign xor_1_out = A ^ B;  // XOR_Gate xor_1, 8 bits wide
  Multiplexer #(.select(3), .width(8), .enable("false")) multiplexer_1 (
    .in0(adder_1_out), .in1(subtractor_1_out), .in2(adder_2_out), .in3(subtractor_2_out), .in4(and_1_out),
    .in5(or_1_out), .in6(not_1_out), .in7(xor_1_out), .out(\output ), .sel(sel));
endmodule
