// Logisim project division by shift.circ as structural Verilog: 4 circuits, main circuit main
module main (
  input  [7:0] A,
  input  [3:0] B
);

  wire [7:0] divider_1_output;
  wire [11:0] n8_bit_hex_to_12_bit_bcd_1_out_2;

  Hex_Digit_Display hex_digit_display_1 (.value(A[7:4]));  // open: dp
  Hex_Digit_Display hex_digit_display_2 (.value(A[3:0]));  // open: dp
  Hex_Digit_Display hex_digit_display_3 (.value(B));  // open: dp
  _8_bit_hex_to_12_bit_bcd u_8_bit_hex_to_12_bit_bcd_1 (
    .in_1(divider_1_output), .out_2(n8_bit_hex_to_12_bit_bcd_1_out_2));
  divider divider_1 (.A(A), .B(B), .\output (divider_1_output));  // open: remainder
  Hex_Digit_Display hex_digit_display_4 (.value(n8_bit_hex_to_12_bit_bcd_1_out_2[11:8]));  // open: dp
  Hex_Digit_Display hex_digit_display_5 (.value(n8_bit_hex_to_12_bit_bcd_1_out_2[3:0]));  // open: dp
  Hex_Digit_Display hex_digit_display_6 (.value(n8_bit_hex_to_12_bit_bcd_1_out_2[7:4]));  // open: dp

  // Notes on the sheet:
  //   /
  //   hex
  //   hex
  //   =
  //   bcd
endmodule

module _8_bit_hex_to_12_bit_bcd (
  input  [7:0] in_1,
  output [11:0] out_2
);

  wire [7:0] divider_1_out;
  wire [7:4] divider_1_rem, divider_2_out, divider_2_rem;

  Hex_Digit_Display hex_digit_display_1 (.value(in_1[7:4]));  // open: dp
  Hex_Digit_Display hex_digit_display_2 (.value(in_1[3:0]));  // open: dp
  Hex_Digit_Display hex_digit_display_3 (.value(out_2[11:8]));  // open: dp
  Divider divider_1 (.a(in_1), .b(8'ha), .out(divider_1_out), .rem({divider_1_rem, out_2[3:0]}));  // open: upper
  Hex_Digit_Display hex_digit_display_4 (.value(out_2[7:4]));  // open: dp
  Hex_Digit_Display hex_digit_display_5 (.value(out_2[3:0]));  // open: dp
  Divider divider_2 (
    .a(divider_1_out), .b(8'ha), .out({divider_2_out, out_2[11:8]}), .rem({divider_2_rem, out_2[7:4]}));  // open: upper
endmodule

module bit_divider (
  input  [7:0] A,
  input  [7:0] B,
  input  [2:0] \bit ,
  output [7:0] \output ,
  output bit_out
);

  wire comparator_1_lt;
  wire [11:0] shifter_1_out, subtractor_1_out;
  wire [11:8] multiplexer_1_out;

  Shifter #(.width(12)) shifter_1 (.in({4'b0000, B}), .\dist ({1'b0, \bit }), .out(shifter_1_out));
  Comparator #(.width(12), .mode("unsigned")) comparator_1 (
    .a({4'b0000, A}), .b(shifter_1_out), .lt(comparator_1_lt));  // open: gt, eq
  Subtractor #(.width(12)) subtractor_1 (
    .a({4'b0000, A}), .b(shifter_1_out), .out(subtractor_1_out));  // open: bin, bout
  Multiplexer #(.width(12), .enable("false")) multiplexer_1 (
    .in0({4'b0000, A}), .in1(subtractor_1_out), .out({multiplexer_1_out, \output }), .sel(bit_out));
  not not_1 (bit_out, comparator_1_lt);
endmodule

module divider (
  input  [7:0] A,
  input  [3:0] B,
  output [7:0] \output ,
  output [3:0] remainder
);

  wire [7:0] bit_divider_1_output, bit_divider_2_output, bit_divider_3_output, bit_divider_4_output,
       bit_divider_5_output, bit_divider_6_output, bit_divider_7_output, multiplier_1_out;
  wire [7:4] subtractor_1_out;

  Hex_Digit_Display hex_digit_display_1 (.value(A[7:4]));  // open: dp
  Hex_Digit_Display hex_digit_display_2 (.value(A[3:0]));  // open: dp
  Hex_Digit_Display hex_digit_display_3 (.value(4'b0000));  // open: dp
  bit_divider bit_divider_1 (
    .A(A), .B({4'b0000, B}), .\bit (3'b111), .\output (bit_divider_1_output), .bit_out(\output [7]));
  Hex_Digit_Display hex_digit_display_4 (.value(B));  // open: dp
  bit_divider bit_divider_2 (
    .A(bit_divider_3_output), .B({4'b0000, B}), .\bit (3'b101), .\output (bit_divider_2_output),
    .bit_out(\output [5]));
  bit_divider bit_divider_3 (
    .A(bit_divider_1_output), .B({4'b0000, B}), .\bit (3'b110), .\output (bit_divider_3_output),
    .bit_out(\output [6]));
  bit_divider bit_divider_4 (
    .A(bit_divider_2_output), .B({4'b0000, B}), .\bit (3'b100), .\output (bit_divider_4_output),
    .bit_out(\output [4]));
  bit_divider bit_divider_5 (
    .A(bit_divider_4_output), .B({4'b0000, B}), .\bit (3'b011), .\output (bit_divider_5_output),
    .bit_out(\output [3]));
  bit_divider bit_divider_6 (
    .A(bit_divider_5_output), .B({4'b0000, B}), .\bit (3'b010), .\output (bit_divider_6_output),
    .bit_out(\output [2]));
  bit_divider bit_divider_7 (
    .A(bit_divider_6_output), .B({4'b0000, B}), .\bit (3'b001), .\output (bit_divider_7_output),
    .bit_out(\output [1]));
  bit_divider bit_divider_8 (
    .A(bit_divider_7_output), .B({4'b0000, B}), .\bit (3'b000), .bit_out(\output [0]));  // open: output
  Hex_Digit_Display hex_digit_display_5 (.value(\output [3:0]));  // open: dp
  Hex_Digit_Display hex_digit_display_6 (.value(\output [7:4]));  // open: dp
  Multiplier multiplier_1 (.a(\output ), .b({4'b0000, B}), .out(multiplier_1_out));  // open: cin, cout
  Subtractor subtractor_1 (.a(A), .b(multiplier_1_out), .out({subtractor_1_out, remainder}));  // open: bin, bout
endmodule
