// Logisim project leftmost bit.circ as structural Verilog: 2 circuits, main circuit main
module main (
  input  [3:0] in_1
);

  wire [3:0] leftmost_bit_1_bit;

  Hex_Digit_Display hex_digit_display_1 (.value(leftmost_bit_1_bit));  // open: dp
  leftmost_bit leftmost_bit_1 (.in(in_1), .\bit (leftmost_bit_1_bit));
endmodule

module leftmost_bit (
  input  [3:0] in,
  output [3:0] \bit 
);

  wire comparator_1_eq, comparator_2_eq, comparator_3_eq, comparator_4_eq;
  wire [3:0] adder_1_out, adder_3_out, multiplexer_1_out, multiplexer_2_out, multiplexer_3_out,
       multiplexer_4_out, shifter_1_out, shifter_2_out;

  Comparator #(.width(4)) comparator_1 (.a(4'b0000), .b(in), .eq(comparator_1_eq));  // open: gt, lt
  Comparator #(.width(4)) comparator_2 (.a(in), .b(4'b0001), .eq(comparator_2_eq));  // open: gt, lt
  Shifter #(.width(4), .shift("lr")) shifter_1 (.in(in), .\dist (2'b01), .out(shifter_1_out));
  Multiplexer #(.width(4), .enable("false")) multiplexer_1 (
    .in0(4'b0000), .in1(4'b1110), .out(multiplexer_1_out), .sel(comparator_1_eq));
  Multiplexer #(.width(4), .enable("false")) multiplexer_2 (
    .in0(4'b0000), .in1(4'b0011), .out(multiplexer_2_out), .sel(comparator_2_eq));
  Comparator #(.width(4)) comparator_3 (.a(shifter_1_out), .b(4'b0001), .eq(comparator_3_eq));  // open: gt, lt
  Shifter #(.width(4), .shift("lr")) shifter_2 (.in(shifter_1_out), .\dist (2'b01), .out(shifter_2_out));
  Multiplexer #(.width(4), .enable("false")) multiplexer_3 (
    .in0(4'b0000), .in1(4'b0010), .out(multiplexer_3_out), .sel(comparator_3_eq));
  Comparator #(.width(4)) comparator_4 (.a(shifter_2_out), .b(4'b0001), .eq(comparator_4_eq));  // open: gt, lt
  Multiplexer #(.width(4), .enable("false")) multiplexer_4 (
    .in0(4'b0000), .in1(4'b0001), .out(multiplexer_4_out), .sel(comparator_4_eq));
  Adder #(.width(4)) adder_1 (.a(multiplexer_1_out), .b(multiplexer_2_out), .out(adder_1_out));  // open: cin, cout
  Adder #(.width(4)) adder_2 (.a(adder_1_out), .b(adder_3_out), .out(\bit ));  // open: cin, cout
  Adder #(.width(4)) adder_3 (.a(multiplexer_3_out), .b(multiplexer_4_out), .out(adder_3_out));  // open: cin, cout
  Hex_Digit_Display hex_digit_display_1 (.value(\bit ));  // open: dp
endmodule
