// Logisim project max of 4 bcd.circ as structural Verilog: 3 circuits, main circuit main
module main (
  input  [3:0] A,
  input  [3:0] B,
  input  [3:0] C,
  input  [3:0] D
);

  wire [3:0] max_of_4_1_out;

  Hex_Digit_Display hex_digit_display_1 (.value(A));  // open: dp
  Hex_Digit_Display hex_digit_display_2 (.value(B));  // open: dp
  max_of_4 max_of_4_1 (.A(A), .B(B), .C(C), .D(D), .out(max_of_4_1_out));
  Hex_Digit_Display hex_digit_display_3 (.value(C));  // open: dp
  Hex_Digit_Display hex_digit_display_4 (.value(D));  // open: dp
  Hex_Digit_Display hex_digit_display_5 (.value(max_of_4_1_out));  // open: dp

  // Notes on the sheet:
  //   max(
  //   ,
  //   ,
  //   ,
  //   This gives the max of A, B, C, and D. If any of them are not valid BCD values, it displays E (error).
  //   ) =
endmodule

module max_of_2 (
  input  [3:0] A,
  input  [3:0] B,
  output [3:0] out
);

  wire comparator_1_gt, comparator_2_gt, comparator_3_gt, or_1_out;
  wire [3:0] multiplexer_1_out;

  Comparator #(.width(4), .mode("unsigned")) comparator_1 (.a(B), .b(A), .gt(comparator_1_gt));  // open: eq, lt
  Comparator #(.width(4), .mode("unsigned")) comparator_2 (.a(B), .b(4'b1001), .gt(comparator_2_gt));  // open: eq, lt
  Comparator #(.width(4), .mode("unsigned")) comparator_3 (.a(A), .b(4'b1001), .gt(comparator_3_gt));  // open: eq, lt
  Multiplexer #(.width(4), .enable("false")) multiplexer_1 (
    .in0(A), .in1(B), .out(multiplexer_1_out), .sel(comparator_1_gt));
  or or_1 (or_1_out, comparator_2_gt, comparator_3_gt);
  Multiplexer #(.width(4), .enable("false")) multiplexer_2 (
    .in0(multiplexer_1_out), .in1(4'b1110), .out(out), .sel(or_1_out));
endmodule

module max_of_4 (
  input  [3:0] A,
  input  [3:0] B,
  input  [3:0] C,
  input  [3:0] D,
  output [3:0] out
);

  wire [3:0] max_of_2_2_out, max_of_2_3_out;

  max_of_2 max_of_2_1 (.A(max_of_2_2_out), .B(max_of_2_3_out), .out(out));
  max_of_2 max_of_2_2 (.A(A), .B(B), .out(max_of_2_2_out));
  max_of_2 max_of_2_3 (.A(C), .B(D), .out(max_of_2_3_out));
endmodule
