// Logisim project multiplication by shift.circ as structural Verilog: 4 circuits, main circuit main
module main (
  input  [7:0] A,
  input  [7:0] B
);

  wire [7:0] multiplier_1_out;
  wire [11:0] n8_bit_hex_to_12_bit_bcd_1_out_2;

  Hex_Digit_Display hex_digit_display_1 (.value(A[7:4]));  // open: dp
  Hex_Digit_Display hex_digit_display_2 (.value(A[3:0]));  // open: dp
  Hex_Digit_Display hex_digit_display_3 (.value(B[7:4]));  // open: dp
  Hex_Digit_Display hex_digit_display_4 (.value(B[3:0]));  // open: dp
  _8_bit_hex_to_12_bit_bcd u_8_bit_hex_to_12_bit_bcd_1 (
    .in_1(multiplier_1_out), .out_2(n8_bit_hex_to_12_bit_bcd_1_out_2));
  multiplier multiplier_1 (.A(A), .B(B), .out(multiplier_1_out));
  Hex_Digit_Display hex_digit_display_5 (.value(n8_bit_hex_to_12_bit_bcd_1_out_2[11:8]));  // open: dp
  Hex_Digit_Display hex_digit_display_6 (.value(n8_bit_hex_to_12_bit_bcd_1_out_2[7:4]));  // open: dp
  Hex_Digit_Display hex_digit_display_7 (.value(n8_bit_hex_to_12_bit_bcd_1_out_2[3:0]));  // open: dp

  // Notes on the sheet:
  //   x
  //   hex
  //   =
  //   hex
  //   bcd
endmodule

module _8_bit_hex_to_12_bit_bcd (
  input  [7:0] in_1,
  output [11:0] out_2
);

  wire [7:0] divider_1_out;
  wire [7:4] divider_1_rem, divider_2_out, divider_2_rem;

  Divider divider_1 (.a(in_1), .b(8'ha), .out(divider_1_out), .rem({divider_1_rem, out_2[3:0]}));  // open: upper
  Divider divider_2 (
    .a(divider_1_out), .b(8'ha), .out({divider_2_out, out_2[11:8]}), .rem({divider_2_rem, out_2[7:4]}));  // open: upper
endmodule

module bit_multiplier (
  input  [2:0] \bit ,
  input  [7:0] A,
  input  [7:0] B,
  output [7:0] out
);

  wire bitselector_1_out, not_1_out;
  wire [7:0] shifter_1_out;

  Shifter shifter_1 (.in(A), .\dist (\bit ), .out(shifter_1_out));
  BitSelector bitselector_1 (.in(B), .out(bitselector_1_out), .sel(\bit ));
  not not_1 (not_1_out, bitselector_1_out);
  Multiplexer #(.width(8), .disabled(0), .enable("false")) multiplexer_1 (
    .in0(shifter_1_out), .in1({8{1'b0}}), .out(out), .sel(not_1_out));
endmodule

module multiplier (
  input  [7:0] A,
  input  [7:0] B,
  output [7:0] out
);

  wire [7:0] adder_1_out, adder_2_out, adder_3_out, adder_4_out, adder_5_out, adder_6_out,
       bit_multiplier_1_out, bit_multiplier_2_out, bit_multiplier_3_out, bit_multiplier_4_out,
       bit_multiplier_5_out, bit_multiplier_6_out, bit_multiplier_7_out, bit_multiplier_8_out;

  bit_multiplier bit_multiplier_1 (.A(A), .B(B), .\bit (3'b000), .out(bit_multiplier_1_out));
  bit_multiplier bit_multiplier_2 (.A(A), .B(B), .\bit (3'b001), .out(bit_multiplier_2_out));
  bit_multiplier bit_multiplier_3 (.A(A), .B(B), .\bit (3'b010), .out(bit_multiplier_3_out));
  bit_multiplier bit_multiplier_4 (.A(A), .B(B), .\bit (3'b011), .out(bit_multiplier_4_out));
  bit_multiplier bit_multiplier_5 (.A(A), .B(B), .\bit (3'b100), .out(bit_multiplier_5_out));
  bit_multiplier bit_multiplier_6 (.A(A), .B(B), .\bit (3'b101), .out(bit_multiplier_6_out));
  bit_multiplier bit_multiplier_7 (.A(A), .B(B), .\bit (3'b110), .out(bit_multiplier_7_out));
  bit_multiplier bit_multiplier_8 (.A(A), .B(B), .\bit (3'b111), .out(bit_multiplier_8_out));
  Adder adder_1 (.a(bit_multiplier_1_out), .b(bit_multiplier_2_out), .out(adder_1_out));  // open: cin, cout
  Adder adder_2 (.a(adder_1_out), .b(adder_3_out), .out(adder_2_out));  // open: cin, cout
  Adder adder_3 (.a(bit_multiplier_3_out), .b(bit_multiplier_4_out), .out(adder_3_out));  // open: cin, cout
  Adder adder_4 (.a(bit_multiplier_5_out), .b(bit_multiplier_6_out), .out(adder_4_out));  // open: cin, cout
  Adder adder_5 (.a(adder_4_out), .b(adder_6_out), .out(adder_5_out));  // open: cin, cout
  Adder adder_6 (.a(bit_multiplier_7_out), .b(bit_multiplier_8_out), .out(adder_6_out));  // open: cin, cout
  Adder adder_7 (.a(adder_2_out), .b(adder_5_out), .out(out));  // open: cin, cout
endmodule
