// Logisim project rightmost bit.circ as structural Verilog: 2 circuits, main circuit main
module main (
  input  [5:0] in_1
);

  wire [3:0] rightmost_bit_1_bit;

  Hex_Digit_Display hex_digit_display_1 (.value(rightmost_bit_1_bit));  // open: dp
  rightmost_bit rightmost_bit_1 (.in(in_1), .\bit (rightmost_bit_1_bit));
endmodule

module rightmost_bit (
  input  [5:0] in,
  output [3:0] \bit 
);

  wire comparator_1_eq, comparator_2_eq, comparator_3_eq, comparator_4_eq, comparator_5_eq, comparator_6_eq;
  wire [3:0] adder_1_out, adder_2_out, adder_3_out, adder_4_out, multiplexer_1_out, multiplexer_2_out,
       multiplexer_3_out, multiplexer_4_out, multiplexer_5_out, multiplexer_6_out;
  wire [5:0] shifter_1_out, shifter_2_out, shifter_3_out, shifter_4_out;

  Hex_Digit_Display hex_digit_display_1 (.value({2'b00, in[5:4]}));  // open: dp
  Hex_Digit_Display hex_digit_display_2 (.value(in[3:0]));  // open: dp
  Comparator #(.width(6)) comparator_1 (.a({6{1'b0}}), .b(in), .eq(comparator_1_eq));  // open: gt, lt
  Comparator #(.width(6)) comparator_2 (.a(in), .b(6'b100000), .eq(comparator_2_eq));  // open: gt, lt
  Shifter #(.width(6)) shifter_1 (.in(in), .\dist (3'b001), .out(shifter_1_out));
  Multiplexer #(.width(4), .enable("false")) multiplexer_1 (
    .in0(4'b0000), .in1(4'b1110), .out(multiplexer_1_out), .sel(comparator_1_eq));
  Multiplexer #(.width(4), .enable("false")) multiplexer_2 (
    .in0(4'b0000), .in1(4'b0101), .out(multiplexer_2_out), .sel(comparator_2_eq));
  Comparator #(.width(6)) comparator_3 (.a(shifter_1_out), .b(6'b100000), .eq(comparator_3_eq));  // open: gt, lt
  Shifter #(.width(6)) shifter_2 (.in(shifter_1_out), .\dist (3'b001), .out(shifter_2_out));
  Shifter #(.width(6)) shifter_3 (.in(shifter_2_out), .\dist (3'b001), .out(shifter_3_out));
  Multiplexer #(.width(4), .enable("false")) multiplexer_3 (
    .in0(4'b0000), .in1(4'b0100), .out(multiplexer_3_out), .sel(comparator_3_eq));
  Comparator #(.width(6)) comparator_4 (.a(shifter_2_out), .b(6'b100000), .eq(comparator_4_eq));  // open: gt, lt
  Shifter #(.width(6)) shifter_4 (.in(shifter_3_out), .\dist (3'b001), .out(shifter_4_out));
  Multiplexer #(.width(4), .enable("false")) multiplexer_4 (
    .in0(4'b0000), .in1(4'b0011), .out(multiplexer_4_out), .sel(comparator_4_eq));
  Multiplexer #(.width(4), .enable("false")) multiplexer_5 (
    .in0(4'b0000), .in1(4'b0010), .out(multiplexer_5_out), .sel(comparator_5_eq));
  Comparator #(.width(6)) comparator_5 (.a(shifter_3_out), .b(6'b100000), .eq(comparator_5_eq));  // open: gt, lt
  Comparator #(.width(6)) comparator_6 (.a(shifter_4_out), .b(6'b100000), .eq(comparator_6_eq));  // open: gt, lt
  Multiplexer #(.width(4), .enable("false")) multiplexer_6 (
    .in0(4'b0000), .in1(4'b0001), .out(multiplexer_6_out), .sel(comparator_6_eq));
  Adder #(.width(4)) adder_1 (.a(multiplexer_1_out), .b(multiplexer_2_out), .out(adder_1_out));  // open: cin, cout
  Adder #(.width(4)) adder_2 (.a(multiplexer_3_out), .b(multiplexer_4_out), .out(adder_2_out));  // open: cin, cout
  Adder #(.width(4)) adder_3 (.a(adder_2_out), .b(adder_4_out), .out(adder_3_out));  // open: cin, cout
  Adder #(.width(4)) adder_4 (.a(multiplexer_5_out), .b(multiplexer_6_out), .out(adder_4_out));  // open: cin, cout
  Hex_Digit_Display hex_digit_display_3 (.value(\bit ));  // open: dp
  Adder #(.width(4)) adder_5 (.a(adder_1_out), .b(adder_3_out), .out(\bit ));  // open: cin, cout
endmodule
